# Fritzing sketch Pin_Configuration (saved by Fritzing 0.9.9b)
breadboards: 1

parts:
  MH-ET_Live_Minikit_for_ESP1 = MH-ET Live Minikit for ESP32
  Bauteil3 = Adafruit MAX98357A I2S 3W Class D Amplifier [part_number="Adafruit #3006"]
  SP1 = SPEAKER [package=pcb_mount_speaker]
  Bauteil5 = Adafruit LIS3DH [part_number="Adafruit #2809"]
  Bauteil4 = GY-VL53L0XV2 Laser Ranger Module

nets:
  N1: MH-ET_Live_Minikit_for_ESP1.IO35, Bauteil3.LRCLK
  N2: MH-ET_Live_Minikit_for_ESP1.IO33, Bauteil3.BCLK
  N3: MH-ET_Live_Minikit_for_ESP1.IO34, Bauteil3.DIN
  VIN: MH-ET_Live_Minikit_for_ESP1.3.3V, Bauteil3.VIN, Bauteil5.VIN, Bauteil4.VCC
  GND: MH-ET_Live_Minikit_for_ESP1.TXD, MH-ET_Live_Minikit_for_ESP1.IO21, MH-ET_Live_Minikit_for_ESP1.GND, Bauteil3.GND, Bauteil3.GAIN, Bauteil5.GND, Bauteil5.SDA, Bauteil4.GND, Bauteil4.SDA
  N4: MH-ET_Live_Minikit_for_ESP1.IO22, Bauteil5.SCL, Bauteil4.SCL
  N5: Bauteil3.VO-, SP1.-
  N6: Bauteil3.VO+, SP1.+

notes:
  I2S Amp
  Distance Sensor
  Motion Sensor

custom parts:
  MH-ET Live Minikit for ESP32: MH-ET Live Minikit for ESP32 ( http://mh.nodebb.com/topic/8/mh-et-live-minikit-for-esp32/2/) PCB footprint is invalid.
  Adafruit MAX98357A I2S 3W Class D Amplifier: Listen to this good news - we now have an all in one digital audio amp breakout board that works incredibly well with the Raspberry Pi! If you're looking for an easy and low cost way to get you digital sound files bumpin' then the MAX08357 I2S Amp Breakout is for you. It takes standard I2S digital audio input and, not only decodes it into analog, but also amplifies it directly into a speaker.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
  Adafruit LIS3DH: The LIS3DH is a very popular low power triple-axis accelerometer. It's low-cost, but has just about every 'extra' you'd want in an accelerometer: Three axis sensing, 10-bit precision ±2g/±4g/±8g/±16g selectable scaling Both I2C (2 possible addresses) and SPI interface options Interrupt output Multiple data rate options 1 Hz to 5Khz As low as 2uA current draw (just the chip itself, not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
  GY-VL53L0XV2 Laser Ranger Module: The GY-VL53L0XV2 is based on the VL53L0X from ST Microelectronics, a time-of-flight ranging system integrated into a compact module.
